# Fritzing sketch calc_fz (saved by Fritzing 0.7.10b)
breadboards: 2

parts:
  Arduino1 = Arduino
  LCD1 = LCD screen
  R1 = Resistor [tolerance=±5% resistance=1k package=THT]
  S9 = Pushbutton [package="[THT]"]
  S10 = Pushbutton [package="[THT]"]
  S11 = Pushbutton [package="[THT]"]
  S12 = Pushbutton [package="[THT]"]
  S13 = Pushbutton [package="[THT]"]
  S16 = Pushbutton [package="[THT]"]
  S17 = Pushbutton [package="[THT]"]
  S18 = Pushbutton [package="[THT]"]
  S19 = Pushbutton [package="[THT]"]
  S20 = Pushbutton [package="[THT]"]
  R2 = Resistor [tolerance=±5% resistance=10k package=THT]
  R3 = Resistor [tolerance=±5% resistance=10k package=THT]
  R4 = Resistor [tolerance=±5% resistance=10k package=THT]
  R5 = Resistor [tolerance=±5% resistance=10k package=THT]
  R8 = Resistor [tolerance=±5% resistance=10k package=THT]
  R11 = Resistor [tolerance=±5% resistance=10k package=THT]
  R12 = Resistor [tolerance=±5% resistance=10k package=THT]
  R13 = Resistor [tolerance=±5% resistance=10k package=THT]
  VCC1 = Battery block 9V
  R10 = Resistor [tolerance=±5% resistance=10k package=THT]
  R9 = Resistor [tolerance=±5% resistance=10k package=THT]

nets:
  N1: Arduino1.D13, S18.Pin_1, S18.Pin_2, R4.Pin_0
  N2: Arduino1.D12, S19.Pin_1, S19.Pin_2, R3.Pin_0
  N3: Arduino1.D11, LCD1.RS
  N4: Arduino1.D10, LCD1.E
  N5: Arduino1.D5, LCD1.DB4
  N6: Arduino1.D4, LCD1.DB5
  N7: Arduino1.D3, LCD1.DB6
  N8: Arduino1.D2, LCD1.DB7
  +5V: Arduino1.+5V, LCD1.VDD, S9.Pin_3, S9.Pin_4, S10.Pin_3, S10.Pin_4, S11.Pin_3, S11.Pin_4, S12.Pin_3, S12.Pin_4, S13.Pin_3, S13.Pin_4, S16.Pin_3, S16.Pin_4, S17.Pin_3, S17.Pin_4, S18.Pin_3, S18.Pin_4, S19.Pin_3, S19.Pin_4, S20.Pin_3, S20.Pin_4, VCC1.+
  GND: Arduino1.GND, LCD1.VSS, LCD1.R/W, R1.Pin_1, R2.Pin_1, R3.Pin_1, R4.Pin_1, R5.Pin_1, R8.Pin_1, R11.Pin_1, R12.Pin_1, R13.Pin_1, VCC1.-, R10.Pin_1, R9.Pin_1
  N9: Arduino1.A0, S20.Pin_1, S20.Pin_2, R2.Pin_0
  N10: Arduino1.A1, S13.Pin_1, S13.Pin_2, R13.Pin_0
  N11: Arduino1.A2, S12.Pin_1, S12.Pin_2, R12.Pin_0
  N12: Arduino1.A3, S11.Pin_1, S11.Pin_2, R11.Pin_0
  N13: Arduino1.A4, S10.Pin_1, S10.Pin_2, R10.Pin_0
  N14: Arduino1.A5, S9.Pin_1, S9.Pin_2, R9.Pin_0
  N15: Arduino1.SCL, S16.Pin_1, S16.Pin_2, R8.Pin_0
  N16: Arduino1.SDA, S17.Pin_1, S17.Pin_2, R5.Pin_0
  N17: LCD1.V0, R1.Pin_0

notes:
  Keypad connector
